// Logisim project 1X4 DEMUX.circ as structural Verilog: 1 circuit, main circuit main
module main (
  input  I,
  input  S0,
  input  S1,
  output Y0,
  output Y1,
  output Y2,
  output Y3
);

  wire not_1_out, not_2_out, not_3_out, not_4_out;

  not not_1 (not_1_out, S1);
  not not_2 (not_2_out, S0);
  not not_3 (not_3_out, S0);
  not not_4 (not_4_out, S1);
  and and_1 (Y0, not_1_out, not_2_out, not_2_out, I);
  and and_2 (Y1, not_3_out, I, S1);
  and and_3 (Y2, S0, S0, not_4_out, I);
  and and_4 (Y3, S0, S1, I);
endmodule
