// Logisim project BINARY DECODER.circ as structural Verilog: 1 circuit, main circuit main
module main (
  input  S0,
  input  s1,
  input  in_3,
  input  in_4,
  input  in_5,
  input  in_6,
  output out_7,
  output out_8
);

  wire and_1_out, and_2_out, and_3_out, and_4_out, not_1_out, not_2_out, not_3_out, not_4_out, not_5_out,
       not_6_out;

  not not_1 (not_1_out, S0);
  not not_2 (not_2_out, s1);
  and and_1 (and_1_out, not_2_out, not_1_out, in_3);
  not not_3 (not_3_out, not_2_out);
  not not_4 (not_4_out, not_1_out);
  not not_5 (not_5_out, not_1_out);
  and and_2 (and_2_out, not_1_out, not_3_out, in_4);
  and and_3 (and_3_out, not_4_out, not_2_out, in_5);
  not not_6 (not_6_out, not_2_out);
  and and_4 (and_4_out, not_6_out, not_5_out, in_6);
  or or_1 (out_7, and_1_out, and_2_out);
  or or_2 (out_8, and_3_out, and_4_out);
endmodule
