// Logisim project FullAdder.circ as structural Verilog: 1 circuit, main circuit main
module main (
  input  X,
  input  Y,
  input  Z,
  output SUM,
  output CARRY
);

  wire and_1_out, and_2_out, or_1_out, xor_1_out;

  or or_1 (or_1_out, Y, Z);
  and and_1 (and_1_out, X, or_1_out);
  xor xor_1 (xor_1_out, X, Y);
  and and_2 (and_2_out, Y, Z);
  xor xor_2 (SUM, xor_1_out, Z);
  or or_2 (CARRY, and_1_out, and_2_out);

  // Notes on the sheet:
  //   x++y
  //   X(Y+Z)
  //   Y+Z
  //   YZ
  //   x++y++z
  //   x(y+z)+yz
endmodule
