// Logisim project FullSubtractor.circ as structural Verilog: 1 circuit, main circuit main
module main (
  input  in_1,
  input  in_2,
  input  in_3,
  output out_4,
  output out_5
);

  wire and_1_out, not_1_out, not_2_out, or_1_out, xor_1_out;

  xor xor_1 (xor_1_out, in_1, in_2);
  not not_1 (not_1_out, in_3);
  not not_2 (not_2_out, in_1);
  or or_1 (or_1_out, not_1_out, not_2_out);
  xor xor_2 (out_4, xor_1_out, in_3);
  and and_1 (and_1_out, in_2, or_1_out);
  or or_2 (out_5, and_1_out, not_2_out);

  // Notes on the sheet:
  //   Y
  //   X'+Z'
  //   x'
  //   X++Y++Z
  //   y(X'+Z')
endmodule
